# Fritzing sketch Untitled Sketch (saved by Fritzing 0.9.3b)
circuit board: 5.19023cm x 4.05455cm
breadboards: 1

parts:
  Componente2 = Arduino Uno (Rev3)
  U1 = Voltage Regulator - 5V [package="TO220 [THT]"]
  VCC1 = Battery block 9V
  U2 = Voltage Regulator - 5V [package="TO220 [THT]"]
  R1 = Trimmer Potentiometer [maximum_resistance=10kΩ package=THT]
  M1 = DC Motor  # not connected

nets:
  N1: Componente2.D6_PWM, U1.input_voltage
  N2: U1.output_voltage, VCC1.-, VCC1.+
  N3: U2.input_voltage, R1.leg1
  N4: U2.GND, R1.wiper
  N5: U2.output_voltage, R1.leg2
